# Fritzing sketch machine_etage (saved by Fritzing 0.9.3b)
breadboards: 1

parts:
  Part1 = Arduino Mega 2560 (Rev3)
  LED1 = LED - 5mm [color="Red (633nm)" package="5 mm [THT]"]  # not connected
  R1 = Resistor [tolerance=±5% resistance=220 package=THT]
  Matrix_keypad1 = KEYPAD 4x4
  M1 = DC Motor
  IC1 = L293D [package=THT]

nets:
  N1: Part1.GND, IC1.0V
  N2: Part1.D13_PWM, IC1.In_1
  N3: Part1.D12_PWM, IC1.In_2
  N4: Part1.D10_PWM, R1.Pin_1
  N5: Part1.D9_PWM, Matrix_keypad1.row4
  N6: Part1.D8_PWM, Matrix_keypad1.row3
  N7: Part1.D2_PWM, Matrix_keypad1.col1
  N8: Part1.D3_PWM, Matrix_keypad1.col2
  N9: Part1.D4_PWM, Matrix_keypad1.col3
  N10: Part1.D5_PWM, Matrix_keypad1.col4
  N11: Part1.D6_PWM, Matrix_keypad1.row1
  N12: Part1.D7_PWM, Matrix_keypad1.row2
  N13: M1.pin_1, IC1.Out_2_(_Controlled_by_Enable_1_)
  N14: M1.pin_2, IC1.Out_1_(_Controlled_by_Enable_1_)
  N15: IC1.Enable_1, IC1.+Vmotor, IC1.+V

notes:
  5V, GRD, Data en Clock gaan verder naar de eerste etage
  ## Machine etage ##
  Krijgt stroom door de 12V barrel connector

custom parts:
  KEYPAD 4x4: Matrix keypad 16 buttons, 4 rows x 4 columns
